# Fritzing sketch Cylon_Pot (saved by Fritzing 0.9.1b)
breadboards: 1

parts:
  LED1 = LED - 5mm [color="Red (633nm)" package="5 mm [THT]"]
  LED2 = LED - 5mm [color="Red (633nm)" package="5 mm [THT]"]
  LED3 = LED - 5mm [color="Red (633nm)" package="5 mm [THT]"]
  LED4 = LED - 5mm [color="Red (633nm)" package="5 mm [THT]"]
  LED5 = LED - 5mm [color="Red (633nm)" package="5 mm [THT]"]
  LED6 = LED - 5mm [color="Red (633nm)" package="5 mm [THT]"]
  R1 = Resistor [tolerance=±5% resistance=220 package=THT]
  R2 = Resistor [tolerance=±5% resistance=220 package=THT]
  R3 = Resistor [tolerance=±5% resistance=220 package=THT]
  R4 = Resistor [tolerance=±5% resistance=220 package=THT]
  R5 = Resistor [tolerance=±5% resistance=220 package=THT]
  R6 = Resistor [tolerance=±5% resistance=220 package=THT]
  Part1 = Arduino Uno (Rev3) - ICSP
  U1 = POT [package=pot_alpha_rv16af-20]  # not connected

nets:
  N1: LED1.cathode, Part1.ICSP_MOSI, Part1.D11_PWM/MOSI
  N2: LED1.anode, R1.Pin_0
  N3: LED2.cathode, Part1.D10_PWM/SS
  N4: LED2.anode, R2.Pin_0
  N5: LED3.cathode, Part1.D9_PWM
  N6: LED3.anode, R3.Pin_0
  N7: LED4.cathode, Part1.D6_PWM
  N8: LED4.anode, R4.Pin_0
  N9: LED5.cathode, Part1.D5_PWM
  N10: LED5.anode, R5.Pin_0
  N11: LED6.cathode, Part1.D3_PWM
  N12: LED6.anode, R6.Pin_0
  N13: R1.Pin_1, R2.Pin_1, R3.Pin_1, R4.Pin_1, R5.Pin_1, R6.Pin_1, Part1.GND
