# Fritzing sketch transSolenoidButton (saved by Fritzing 0.9.3b)
circuit board: 8.46667cm x 5.64444cm
breadboards: 1

parts:
  Part1 = Arduino Uno (Rev3)
  LED1 = LED - 5mm [color="Red (633nm)" package="5 mm [THT]"]
  R1 = Resistor [tolerance=±5% resistance=220 package=THT]
  S1 = Pushbutton [package=THT]
  L1 = Solenoid
  R3 = Resistor [tolerance=±5% resistance=1k package=THT]
  D1 = Rectifier Diode [part_number=1N4148 package="300 mil [THT]"]
  Power_plug2 = Power plug
  Q4 = npn-Powertransistor [part_number=TIP-122 package="TO220 [THT]"]

nets:
  N1: Part1.D12/MISO, S1.leg0
  GND: Part1.GND, R1.Pin_1, S1.leg1, Power_plug2.GND, Q4.emitter
  N2: Part1.D6_PWM, LED1.anode, R3.Pin_0
  N3: LED1.cathode, R1.Pin_0
  N4: L1.pin1, D1.anode, Q4.collector
  N5: L1.pin2, D1.cathode, Power_plug2.VCC
  N6: R3.Pin_1, Q4.base
