# Fritzing sketch LostRedditButton (saved by Fritzing 0.9.3b)
circuit board: 6.88566cm x 5.36311cm
breadboards: 1

parts:
  Arduino1 = Arduino Uno (Rev3)
  S2 = Pushbutton [package=THT]
  LED2 = LED - 5mm [color="Yellow (592nm)" package="5 mm [THT]"]
  LED1 = LED - 5mm [color="Red (633nm)" package="5 mm [THT]"]
  R1 = Resistor [tolerance=±5% resistance=220 package=THT]
  R2 = Resistor [tolerance=±5% resistance=220 package=THT]

nets:
  N1: Arduino1.D11_PWM/MOSI, LED2.anode
  N2: Arduino1.D12/MISO, LED1.anode
  N3: Arduino1.GND, S2.leg1, R1.Pin_1, R2.Pin_1
  N4: Arduino1.D4, S2.leg0
  N5: LED2.cathode, R2.Pin_0
  N6: LED1.cathode, R1.Pin_0

// code stored in the sketch: TrafficLight_0.ino
void setup()
{

}


void loop()
{
  
}
