# Fritzing sketch TrafficLight_1 (saved by Fritzing 0.9.1b)
circuit board: 6.88566cm x 5.36311cm
breadboards: 1

parts:
  LED1 = LED - 5mm [color="Red (633nm)" package="5 mm [THT]"]
  LED2 = LED - 5mm [color="Yellow (592nm)" package="5 mm [THT]"]
  LED3 = LED - 5mm [color="Green (555nm)" package="5 mm [THT]"]
  R1 = Resistor [tolerance=±5% resistance=220 package=THT]
  R2 = Resistor [tolerance=±5% resistance=220 package=THT]
  R3 = Resistor [tolerance=±5% resistance=220 package=THT]
  Arduino1 = Arduino Uno (Rev3)
  LED4 = LED - 5mm [color="Red (633nm)" package="5 mm [THT]"]
  LED5 = LED - 5mm [color="White (8000K)" package="5 mm [THT]"]
  R5 = Resistor [tolerance=±5% resistance=220 package=THT]
  R6 = Resistor [tolerance=±5% resistance=220 package=THT]
  S2 = Pushbutton [package=THT]
  R7 = Resistor [tolerance=±5% resistance=10k package=THT]

nets:
  N1: LED1.cathode, R1.Pin_0
  N2: LED1.anode, Arduino1.D12/MISO
  N3: LED2.cathode, R2.Pin_0
  N4: LED2.anode, Arduino1.D11_PWM/MOSI
  N5: LED3.cathode, R3.Pin_0
  N6: LED3.anode, Arduino1.D10_PWM/SS
  N7: R1.Pin_1, R2.Pin_1, R3.Pin_1, Arduino1.GND, R5.Pin_1, R6.Pin_1, R7.Pin_1
  N8: Arduino1.D2, LED5.anode
  N9: Arduino1.D3_PWM, LED4.anode
  N10: Arduino1.D4, S2.leg0, R7.Pin_0
  N11: Arduino1.5V, S2.leg1
  N12: LED4.cathode, R6.Pin_0
  N13: LED5.cathode, R5.Pin_0

// code stored in the sketch: TrafficLight_0.ino
void setup()
{

}


void loop()
{
  
}
