# Fritzing sketch LED_0 (saved by Fritzing 0.9.1b)
circuit board: 6.88566cm x 5.36311cm
breadboards: 1

parts:
  LED1 = LED - 5mm [color="Red (633nm)" package="5 mm [THT]"]
  R1 = Resistor [tolerance=±5% resistance=220 package=THT]
  Arduino1 = Arduino Uno (Rev3)

nets:
  N1: LED1.cathode, R1.Pin_0
  N2: LED1.anode, Arduino1.D12/MISO
  N3: R1.Pin_1, Arduino1.GND

// code stored in the sketch: TrafficLight_0.ino
void setup()
{

}


void loop()
{
  
}
